# Fritzing sketch ElectricityMeter_with_DS1307 (saved by Fritzing 0.9.3b)
breadboards: 1

parts:
  Part1 = Real Time Clock Module - DS1307 RTC Breakout Board
  Part2 = Arduino Uno (Rev3)

nets:
  5V: Part1.5V, Part2.5V
  GND: Part1.GND, Part2.GND
  N1: Part1.SCL, Part2.A5/SCL
  N2: Part1.SDA, Part2.A4/SDA
